// Digital circuit main.dig as structural Verilog
module main (
);

  Seven_Seg seven_seg_1 ();  // open: a, b, c, d, e, f, g, dp
  Seven_Seg seven_seg_2 ();  // open: a, b, c, d, e, f, g, dp
  Seven_Seg seven_seg_3 ();  // open: a, b, c, d, e, f, g, dp
  Seven_Seg seven_seg_4 ();  // open: a, b, c, d, e, f, g, dp
  Seven_Seg seven_seg_5 ();  // open: a, b, c, d, e, f, g, dp
  Seven_Seg seven_seg_6 ();  // open: a, b, c, d, e, f, g, dp
endmodule
